// Logisim project sap1.circ as structural Verilog
module main (
  input  auto_clock,
  input  manual_input,
  input  ram_load,
  input  a3,
  input  a2,
  input  a1,
  input  a0,
  input  d7,
  input  d6,
  input  d5,
  input  d4,
  input  d3,
  input  d2,
  input  d1,
  input  d0
);

  wire accumulator_1_a_alu0, accumulator_1_a_alu1, accumulator_1_a_alu2, accumulator_1_a_alu3,
       accumulator_1_a_alu4, accumulator_1_a_alu5, accumulator_1_a_alu6, accumulator_1_a_alu7, alu_1_zf,
       and_1_out, and_2_out, clk_1_clock_out, clock_1_out, control_unit_1_a_load, control_unit_1_a_store,
       control_unit_1_add_sub, control_unit_1_alu_store, control_unit_1_b_load, control_unit_1_halt,
       control_unit_1_ir_load, control_unit_1_ir_store, control_unit_1_mar_load, control_unit_1_out_load,
       control_unit_1_pc_inc, control_unit_1_pc_load, control_unit_1_pc_store, control_unit_1_ram_load,
       control_unit_1_ram_store, ir_1_op0, ir_1_op1, ir_1_op2, ir_1_op3, manual_tick_out, mar_1_mar_out0,
       mar_1_mar_out1, mar_1_mar_out2, mar_1_mar_out3, multiplexer_1_out, not_1_out, not_2_out,
       out_register_1_o0, out_register_1_o1, out_register_1_o2, out_register_1_o3, out_register_1_o4,
       out_register_1_o5, out_register_1_o6, out_register_1_o7, pc_1_out_10, pc_1_out_11, pc_1_out_12,
       pc_1_out_13, ram16x8_1_q4, ram16x8_1_q5, ram16x8_1_q6, ram16x8_1_q7, reset_out, temp_register_1_bo0,
       temp_register_1_bo1, temp_register_1_bo2, temp_register_1_bo3, temp_register_1_bo4,
       temp_register_1_bo5, temp_register_1_bo6, temp_register_1_bo7, zf_1_to_cu, zf_1_zero;

  Multiplexer multiplexer_1 (
    .in0(control_unit_1_ram_load), .in1(ram_load), .out(multiplexer_1_out), .sel(manual_input));
  Clock clock_1 (.out(clock_1_out));
  Button manual_tick (.out(manual_tick_out));
  Button reset (.out(reset_out));
  LED led_1 (.in(out_register_1_o7));
  LED led_2 (.in(out_register_1_o6));
  LED led_3 (.in(out_register_1_o5));
  LED led_4 (.in(out_register_1_o4));
  LED led_5 (.in(out_register_1_o3));
  LED led_6 (.in(out_register_1_o2));
  CLK clk_1 (
    .clock(clock_1_out), .manual_auto(auto_clock), .manual_tick(manual_tick_out), .halt(control_unit_1_halt),
    .clock_out(clk_1_clock_out));
  LED led_7 (.in(out_register_1_o1));
  LED led_8 (.in(out_register_1_o0));
  not not_1 (not_1_out, manual_input);
  and and_1 (and_1_out, not_1_out, clk_1_clock_out);
  PC pc_1 (
    .a0(pc_1_out_10), .a1(pc_1_out_11), .a2(pc_1_out_12), .a3(pc_1_out_13), .reset(reset_out),
    .pc_load(control_unit_1_pc_load), .pc_inc(control_unit_1_pc_inc), .clk(and_1_out),
    .pc_store(control_unit_1_pc_store), .out_10(pc_1_out_10), .out_11(pc_1_out_11), .out_12(pc_1_out_12),
    .out_13(pc_1_out_13));
  MAR mar_1 (
    .mar_in0(pc_1_out_10), .mar_in1(pc_1_out_11), .mar_in2(pc_1_out_12), .mar_in3(pc_1_out_13),
    .mar_load(control_unit_1_mar_load), .clk(clk_1_clock_out), .reset(reset_out), .mar_out0(mar_1_mar_out0),
    .mar_out1(mar_1_mar_out1), .mar_out2(mar_1_mar_out2), .mar_out3(mar_1_mar_out3));
  RAM16x8 ram16x8_1 (
    .a0(mar_1_mar_out0), .a1(mar_1_mar_out1), .a2(mar_1_mar_out2), .a3(mar_1_mar_out3), .ia0(a0), .ia1(a1),
    .ia2(a2), .ia3(a3), .e0(pc_1_out_10), .e1(pc_1_out_11), .e2(pc_1_out_12), .e3(pc_1_out_13),
    .e4(ram16x8_1_q4), .e5(ram16x8_1_q5), .e6(ram16x8_1_q6), .e7(ram16x8_1_q7), .d0(d0), .d1(d1), .d2(d2),
    .d3(d3), .d4(d4), .d5(d5), .d6(d6), .d7(d7), .ram_store(control_unit_1_ram_store), .clk(clk_1_clock_out),
    .ram_load(multiplexer_1_out), .manual(manual_input), .q0(pc_1_out_10), .q1(pc_1_out_11),
    .q2(pc_1_out_12), .q3(pc_1_out_13), .q4(ram16x8_1_q4), .q5(ram16x8_1_q5), .q6(ram16x8_1_q6),
    .q7(ram16x8_1_q7));
  IR ir_1 (
    .d3(pc_1_out_13), .d4(ram16x8_1_q4), .d5(ram16x8_1_q5), .d6(ram16x8_1_q6), .d7(ram16x8_1_q7),
    .d0(pc_1_out_10), .d1(pc_1_out_11), .d2(pc_1_out_12), .ir_load(control_unit_1_ir_load),
    .clk(clk_1_clock_out), .reset(reset_out), .ir_store(control_unit_1_ir_store), .a2(pc_1_out_12),
    .a3(pc_1_out_13), .op0(ir_1_op0), .op1(ir_1_op1), .op2(ir_1_op2), .op3(ir_1_op3), .a0(pc_1_out_10),
    .a1(pc_1_out_11));
  CONTROL_UNIT control_unit_1 (
    .reset(reset_out), .clk(and_2_out), .zf(zf_1_to_cu), .op0(ir_1_op0), .op1(ir_1_op1), .op2(ir_1_op2),
    .op3(ir_1_op3), .add_sub(control_unit_1_add_sub), .a_load(control_unit_1_a_load),
    .a_store(control_unit_1_a_store), .alu_store(control_unit_1_alu_store), .b_load(control_unit_1_b_load),
    .out_load(control_unit_1_out_load), .halt(control_unit_1_halt), .pc_load(control_unit_1_pc_load),
    .mar_load(control_unit_1_mar_load), .ram_load(control_unit_1_ram_load),
    .ram_store(control_unit_1_ram_store), .ir_load(control_unit_1_ir_load),
    .ir_store(control_unit_1_ir_store), .pc_store(control_unit_1_pc_store), .pc_inc(control_unit_1_pc_inc));
  and and_2 (and_2_out, clk_1_clock_out, not_2_out);
  not not_2 (not_2_out, manual_input);
  LED led_9 (.in(ram16x8_1_q7));
  LED led_10 (.in(ram16x8_1_q6));
  LED led_11 (.in(ram16x8_1_q5));
  LED led_12 (.in(ram16x8_1_q4));
  Pull_Resistor pull_resistor_1 (.node(ram16x8_1_q7));
  Pull_Resistor pull_resistor_2 (.node(ram16x8_1_q6));
  Pull_Resistor pull_resistor_3 (.node(ram16x8_1_q5));
  Pull_Resistor pull_resistor_4 (.node(ram16x8_1_q4));
  LED led_13 (.in(pc_1_out_13));
  LED led_14 (.in(pc_1_out_12));
  LED led_15 (.in(pc_1_out_11));
  LED led_16 (.in(pc_1_out_10));
  Pull_Resistor pull_resistor_5 (.node(pc_1_out_13));
  Pull_Resistor pull_resistor_6 (.node(pc_1_out_12));
  Pull_Resistor pull_resistor_7 (.node(pc_1_out_11));
  Pull_Resistor pull_resistor_8 (.node(pc_1_out_10));
  ACCUMULATOR accumulator_1 (
    .a_load(control_unit_1_a_load), .clk(clk_1_clock_out), .reset(reset_out),
    .a_store(control_unit_1_a_store), .a_in6(ram16x8_1_q6), .a_in7(ram16x8_1_q7), .a_in0(pc_1_out_10),
    .a_in1(pc_1_out_11), .a_in2(pc_1_out_12), .a_in3(pc_1_out_13), .a_in4(ram16x8_1_q4),
    .a_in5(ram16x8_1_q5), .a_out0(pc_1_out_10), .a_out1(pc_1_out_11), .a_out2(pc_1_out_12),
    .a_out3(pc_1_out_13), .a_out4(ram16x8_1_q4), .a_out5(ram16x8_1_q5), .a_out6(ram16x8_1_q6),
    .a_out7(ram16x8_1_q7), .a_alu0(accumulator_1_a_alu0), .a_alu1(accumulator_1_a_alu1),
    .a_alu2(accumulator_1_a_alu2), .a_alu3(accumulator_1_a_alu3), .a_alu4(accumulator_1_a_alu4),
    .a_alu5(accumulator_1_a_alu5), .a_alu6(accumulator_1_a_alu6), .a_alu7(accumulator_1_a_alu7));
  TEMP_REGISTER temp_register_1 (
    .d0(pc_1_out_10), .d1(pc_1_out_11), .d2(pc_1_out_12), .d3(pc_1_out_13), .d4(ram16x8_1_q4),
    .d5(ram16x8_1_q5), .d6(ram16x8_1_q6), .d7(ram16x8_1_q7), .b_load(control_unit_1_b_load),
    .clk(clk_1_clock_out), .reset(reset_out), .bo0(temp_register_1_bo0), .bo1(temp_register_1_bo1),
    .bo2(temp_register_1_bo2), .bo3(temp_register_1_bo3), .bo4(temp_register_1_bo4),
    .bo5(temp_register_1_bo5), .bo6(temp_register_1_bo6), .bo7(temp_register_1_bo7));
  ALU alu_1 (
    .sub(control_unit_1_add_sub), .alu_store(control_unit_1_alu_store), .a0(accumulator_1_a_alu0),
    .a1(accumulator_1_a_alu1), .a2(accumulator_1_a_alu2), .a3(accumulator_1_a_alu3),
    .a4(accumulator_1_a_alu4), .a5(accumulator_1_a_alu5), .a6(accumulator_1_a_alu6),
    .a7(accumulator_1_a_alu7), .b0(temp_register_1_bo0), .b1(temp_register_1_bo1), .b2(temp_register_1_bo2),
    .b3(temp_register_1_bo3), .b4(temp_register_1_bo4), .b5(temp_register_1_bo5), .b6(temp_register_1_bo6),
    .b7(temp_register_1_bo7), .ao0(pc_1_out_10), .ao1(pc_1_out_11), .ao2(pc_1_out_12), .ao3(pc_1_out_13),
    .ao4(ram16x8_1_q4), .ao5(ram16x8_1_q5), .ao6(ram16x8_1_q6), .ao7(ram16x8_1_q7), .zf(alu_1_zf));
  OUT_REGISTER out_register_1 (
    .d1(pc_1_out_11), .d2(pc_1_out_12), .d3(pc_1_out_13), .d4(ram16x8_1_q4), .d5(ram16x8_1_q5),
    .d6(ram16x8_1_q6), .d7(ram16x8_1_q7), .d0(pc_1_out_10), .out_load(control_unit_1_out_load),
    .clk(clk_1_clock_out), .reset(reset_out), .o1(out_register_1_o1), .o2(out_register_1_o2),
    .o3(out_register_1_o3), .o4(out_register_1_o4), .o5(out_register_1_o5), .o6(out_register_1_o6),
    .o7(out_register_1_o7), .o0(out_register_1_o0));
  LED zero (.in(zf_1_zero));
  ZF zf_1 (.alu(alu_1_zf), .clk(clk_1_clock_out), .reset(reset_out), .zero(zf_1_zero), .to_cu(zf_1_to_cu));
endmodule

module PC (
  input  reset,
  input  pc_load,
  input  pc_inc,
  input  clk,
  input  pc_store,
  input  a0,
  input  a1,
  input  a2,
  input  a3,
  output out_10,
  output out_11,
  output out_12,
  output out_13
);

  wire not_1_out;
  wire [3:0] counter_1_q;

  Counter #(.max('hf), .width(4)) counter_1 (
    .clr(reset), .load(pc_load), .up(pc_inc), .count(pc_inc), .clk(not_1_out), .D({a3, a2, a1, a0}),
    .Q(counter_1_q));  // open: carry
  not not_1 (not_1_out, clk);
  assign {out_13, out_12, out_11, out_10} = pc_store ? counter_1_q : 4'bz;  // Controlled_Buffer controlled_buffer_1
endmodule

module IR (
  input  d0,
  input  d1,
  input  d2,
  input  d3,
  input  d4,
  input  d5,
  input  d6,
  input  d7,
  input  ir_load,
  input  clk,
  input  reset,
  input  ir_store,
  output a0,
  output a1,
  output a2,
  output a3,
  output op0,
  output op1,
  output op2,
  output op3
);

  wire not_1_out;
  wire [3:0] register_1_q;

  Register register_1 (
    .D({d7, d6, d5, d4, d3, d2, d1, d0}), .en(ir_load), .clk(not_1_out),
    .Q({op3, op2, op1, op0, register_1_q}), .clr(reset));
  not not_1 (not_1_out, clk);
  assign {a3, a2, a1, a0} = ir_store ? register_1_q : 4'bz;  // Controlled_Buffer controlled_buffer_1
endmodule

module MAR (
  input  mar_in0,
  input  mar_in1,
  input  mar_in2,
  input  mar_in3,
  input  mar_load,
  input  clk,
  input  reset,
  output mar_out0,
  output mar_out1,
  output mar_out2,
  output mar_out3
);

  wire [3:0] controlled_buffer_1_out;

  assign controlled_buffer_1_out = mar_load ? {mar_in3, mar_in2, mar_in1, mar_in0} : 4'bz;  // Controlled_Buffer controlled_buffer_1
  Register #(.width(4)) register_1 (
    .D(controlled_buffer_1_out), .en(mar_load), .clk(clk), .Q({mar_out3, mar_out2, mar_out1, mar_out0}),
    .clr(reset));
endmodule

module RAM16x8 (
  input  a0,
  input  a1,
  input  a2,
  input  a3,
  input  ia0,
  input  ia1,
  input  ia2,
  input  ia3,
  input  ram_store,
  input  clk,
  input  ram_load,
  input  e0,
  input  manual,
  input  e1,
  input  e2,
  input  e3,
  input  e4,
  input  e5,
  input  e6,
  input  e7,
  input  d0,
  input  d1,
  input  d2,
  input  d3,
  input  d4,
  input  d5,
  input  d6,
  input  d7,
  output q0,
  output q1,
  output q2,
  output q3,
  output q4,
  output q5,
  output q6,
  output q7
);

  wire not_1_out;
  wire [3:0] or_1_out;
  wire [7:0] multiplexer_1_out, ram_1_dout;

  RAM #(.addrWidth(4)) ram_1 (
    .addr(or_1_out), .we(ram_load), .oe(1'b1), .clk(not_1_out), .din(multiplexer_1_out), .dout(ram_1_dout));
  assign or_1_out = {a3, a2, a1, a0} | {ia3, ia2, ia1, ia0};  // OR_Gate or_1, 4 bits wide
  not not_1 (not_1_out, clk);
  Multiplexer #(.width(8)) multiplexer_1 (
    .in0({e7, e6, e5, e4, e3, e2, e1, e0}), .in1({d7, d6, d5, d4, d3, d2, d1, d0}), .out(multiplexer_1_out),
    .sel(manual));
  assign {q7, q6, q5, q4, q3, q2, q1, q0} = ram_store ? ram_1_dout : 8'bz;  // Controlled_Buffer controlled_buffer_1
endmodule

module ALU (
  input  a0,
  input  a1,
  input  a2,
  input  a3,
  input  a4,
  input  a5,
  input  a6,
  input  a7,
  input  sub,
  input  alu_store,
  input  b0,
  input  b1,
  input  b2,
  input  b3,
  input  b4,
  input  b5,
  input  b6,
  input  b7,
  output ao0,
  output ao1,
  output ao2,
  output ao3,
  output ao4,
  output ao5,
  output ao6,
  output ao7,
  output zf
);

  wire [7:0] adder_1_out, bit_extender_1_out, xor_1_out;

  assign bit_extender_1_out = {{7{sub}}, sub};  // Bit_Extender bit_extender_1
  assign xor_1_out = bit_extender_1_out ^ {b7, b6, b5, b4, b3, b2, b1, b0};  // XOR_Gate xor_1, 8 bits wide
  assign {ao7, ao6, ao5, ao4, ao3, ao2, ao1, ao0} = alu_store ? adder_1_out : 8'bz;  // Controlled_Buffer controlled_buffer_1
  Adder adder_1 (.a({a7, a6, a5, a4, a3, a2, a1, a0}), .b(xor_1_out), .out(adder_1_out), .cin(sub));  // open: cout
  nor nor_1 (zf, ao0, ao1, ao2, ao3, ao4, ao5, ao6, ao7);
endmodule

module ACCUMULATOR (
  input  a_in0,
  input  a_in1,
  input  a_load,
  input  clk,
  input  a_in2,
  input  reset,
  input  a_in3,
  input  a_store,
  input  a_in4,
  input  a_in5,
  input  a_in6,
  input  a_in7,
  output a_out0,
  output a_out1,
  output a_out2,
  output a_out3,
  output a_out4,
  output a_out5,
  output a_out6,
  output a_out7,
  output a_alu0,
  output a_alu1,
  output a_alu2,
  output a_alu3,
  output a_alu4,
  output a_alu5,
  output a_alu6,
  output a_alu7
);

  Register register_1 (
    .D({a_in7, a_in6, a_in5, a_in4, a_in3, a_in2, a_in1, a_in0}), .en(a_load), .clk(clk),
    .Q({a_alu7, a_alu6, a_alu5, a_alu4, a_alu3, a_alu2, a_alu1, a_alu0}), .clr(reset));
  assign {a_out7, a_out6, a_out5, a_out4, a_out3, a_out2, a_out1, a_out0} = a_store ? {a_alu7, a_alu6, a_alu5, a_alu4, a_alu3, a_alu2, a_alu1, a_alu0} : 8'bz;  // Controlled_Buffer controlled_buffer_1
endmodule

module OUT_REGISTER (
  input  d0,
  input  d1,
  input  d2,
  input  d3,
  input  d4,
  input  d5,
  input  d6,
  input  d7,
  input  out_load,
  input  clk,
  input  reset,
  output o0,
  output o1,
  output o2,
  output o3,
  output o4,
  output o5,
  output o6,
  output o7
);

  wire not_1_out;

  not not_1 (not_1_out, clk);
  Register register_1 (
    .D({d7, d6, d5, d4, d3, d2, d1, d0}), .en(out_load), .clk(not_1_out),
    .Q({o7, o6, o5, o4, o3, o2, o1, o0}), .clr(reset));
endmodule

module TEMP_REGISTER (
  input  d0,
  input  d1,
  input  d2,
  input  d3,
  input  d4,
  input  d5,
  input  d6,
  input  d7,
  input  b_load,
  input  clk,
  input  reset,
  output bo0,
  output bo1,
  output bo2,
  output bo3,
  output bo4,
  output bo5,
  output bo6,
  output bo7
);

  Register register_1 (
    .D({d7, d6, d5, d4, d3, d2, d1, d0}), .en(b_load), .clk(clk),
    .Q({bo7, bo6, bo5, bo4, bo3, bo2, bo1, bo0}), .clr(reset));
endmodule

module OPCODE_DECODER (
  input  op0,
  input  op1,
  input  op2,
  input  op3,
  output LDA,
  output ADD,
  output SUB,
  output STA,
  output JMP,
  output JZ,
  output OUTT,
  output HALT
);

  wire not_1_out, not_2_out, pull_resistor_5_node, pull_resistor_6_node;

  Pull_Resistor pull_resistor_1 (.node(op3));
  Pull_Resistor pull_resistor_2 (.node(op2));
  Pull_Resistor pull_resistor_3 (.node(op1));
  Pull_Resistor pull_resistor_4 (.node(op0));
  Pull_Resistor pull_resistor_5 (.node(pull_resistor_5_node));
  Pull_Resistor pull_resistor_6 (.node(pull_resistor_6_node));
  not not_1 (not_1_out, op0);
  not not_2 (not_2_out, op1);
  not not_3 (pull_resistor_6_node, op2);
  not not_4 (pull_resistor_5_node, op3);
  Pull_Resistor pull_resistor_7 (.node(not_2_out));
  Pull_Resistor pull_resistor_8 (.node(not_1_out));
  Pull_Resistor pull_resistor_9 (.node(not_1_out));
  Pull_Resistor pull_resistor_10 (.node(not_2_out));
  Pull_Resistor pull_resistor_11 (.node(pull_resistor_6_node));
  Pull_Resistor pull_resistor_12 (.node(pull_resistor_5_node));
  and and_1 (LDA, not_1_out, not_2_out, pull_resistor_6_node, pull_resistor_5_node);
  and and_2 (ADD, op0, not_2_out, pull_resistor_6_node, pull_resistor_5_node);
  and and_3 (SUB, not_1_out, op1, pull_resistor_6_node, pull_resistor_5_node);
  and and_4 (STA, op0, op1, pull_resistor_6_node, pull_resistor_5_node);
  and and_5 (JMP, not_1_out, not_2_out, op2, pull_resistor_5_node);
  and and_6 (JZ, op0, not_2_out, op2, pull_resistor_5_node);
  and and_7 (OUTT, not_1_out, op1, op2, op3);
  and and_8 (HALT, op0, op1, op2, op3);
endmodule

module STATE_COUNTER (
  input  reset,
  input  clk,
  output t1,
  output t2,
  output t3,
  output t4,
  output t5,
  output t6
);

  wire and_7_out, not_1_out, not_2_out, not_3_out, or_1_out;
  wire [2:0] counter_1_q;

  or or_1 (or_1_out, reset, and_7_out);
  Counter #(.max('h7), .width(3)) counter_1 (
    .clr(or_1_out), .load(1'b0), .up(1'b1), .count(1'b1), .clk(clk), .Q(counter_1_q));  // open: D, carry
  not not_1 (not_1_out, counter_1_q[0]);
  not not_2 (not_2_out, counter_1_q[1]);
  not not_3 (not_3_out, counter_1_q[2]);
  and and_1 (t1, not_1_out, not_2_out, not_3_out);
  and and_2 (t2, counter_1_q[0], not_2_out, not_3_out);
  and and_3 (t3, not_1_out, counter_1_q[1], not_3_out);
  and and_4 (t4, counter_1_q[0], counter_1_q[1], not_3_out);
  and and_5 (t5, not_1_out, not_2_out, counter_1_q[2]);
  and and_6 (t6, counter_1_q[0], not_2_out, counter_1_q[2]);
  and and_7 (and_7_out, not_1_out, counter_1_q[1], counter_1_q[2]);
endmodule

module CLK (
  input  clock,
  input  manual_auto,
  input  manual_tick,
  input  halt,
  output clock_out
);

  wire and_1_out, and_2_out, not_1_out, not_2_out, or_1_out;

  not not_1 (not_1_out, manual_auto);
  and and_1 (and_1_out, clock, manual_auto);
  and and_2 (and_2_out, not_1_out, manual_tick);
  or or_1 (or_1_out, and_1_out, and_2_out);
  not not_2 (not_2_out, halt);
  and and_3 (clock_out, or_1_out, not_2_out);
endmodule

module CONTROL_UNIT (
  input  op0,
  input  op1,
  input  op2,
  input  op3,
  input  reset,
  input  clk,
  input  zf,
  output pc_store,
  output pc_inc,
  output pc_load,
  output mar_load,
  output ram_load,
  output ram_store,
  output ir_load,
  output ir_store,
  output a_load,
  output a_store,
  output add_sub,
  output alu_store,
  output b_load,
  output out_load,
  output halt
);

  wire add, and_1_out, and_2_out, and_3_out, and_4_out, and_5_out, and_6_out, and_7_out, and_8_out,
       and_9_out, and_10_out, and_11_out, and_12_out, and_13_out, and_14_out, and_16_out, and_17_out,
       and_18_out, and_19_out, and_20_out, and_21_out, and_23_out, and_24_out, and_25_out, and_26_out, jmp,
       jz, lda, or_3_out, or_5_out, outt, sta, sub, t4, t5, t6;

  OPCODE_DECODER opcode_decoder_1 (
    .op0(op0), .op1(op1), .op2(op2), .op3(op3), .LDA(lda), .ADD(add), .SUB(sub), .STA(sta), .JMP(jmp),
    .JZ(jz), .OUTT(outt), .HALT(halt));
  STATE_COUNTER state_counter_1 (
    .reset(reset), .clk(clk), .t1(pc_store), .t2(pc_inc), .t3(ir_load), .t4(t4), .t5(t5), .t6(t6));
  and and_1 (and_1_out, lda, t4);
  and and_2 (and_2_out, sub, t4);
  and and_3 (and_3_out, add, t4);
  and and_4 (and_4_out, sta, t4);
  and and_5 (and_5_out, lda, t5);
  and and_6 (and_6_out, sub, t5);
  and and_7 (and_7_out, add, t5);
  and and_8 (and_8_out, lda, t4);
  and and_9 (and_9_out, sub, t4);
  and and_10 (and_10_out, sta, t4);
  and and_11 (and_11_out, add, t4);
  and and_12 (and_12_out, jmp, t4);
  and and_13 (and_13_out, jmp, t4);
  or or_1 (pc_load, and_13_out, and_14_out);
  and and_14 (and_14_out, jz, zf, t4);
  or or_2 (mar_load, pc_store, or_3_out);
  or or_3 (or_3_out, and_1_out, and_2_out, and_3_out, and_4_out);
  and and_15 (ram_load, t5, sta);
  or or_4 (ram_store, ir_load, or_5_out);
  or or_5 (or_5_out, and_5_out, and_6_out, and_7_out);
  and and_16 (and_16_out, zf, jz, t4);
  or or_6 (ir_store, and_8_out, and_9_out, and_16_out, and_10_out, and_11_out, and_12_out);
  and and_17 (and_17_out, lda, t5);
  and and_18 (and_18_out, sub, t6);
  or or_7 (a_load, and_17_out, and_18_out, and_19_out);
  and and_19 (and_19_out, add, t6);
  and and_20 (and_20_out, t4, outt);
  or or_8 (a_store, and_20_out, and_21_out);
  and and_21 (and_21_out, t5, sta);
  and and_22 (add_sub, sub, t6);
  and and_23 (and_23_out, add, t6);
  or or_9 (alu_store, and_23_out, and_24_out);
  and and_24 (and_24_out, sub, t6);
  and and_25 (and_25_out, add, t5);
  or or_10 (b_load, and_25_out, and_26_out);
  and and_26 (and_26_out, sub, t5);
  and and_27 (out_load, t4, outt);

  // Other names for the same wires on the sheet: t1 = pc_store; t2 = pc_inc; t3 = ir_load
endmodule

module USER_INPUT (
  input  WRITE,
  input  LDA_RESET,
  input  ADD,
  input  SUB,
  input  OUTT,
  input  HALT,
  output ram_write,
  output d0,
  output d1,
  output d2,
  output d3
);

  wire and_1_out, and_2_out, and_3_out, and_4_out, not_1_out, not_2_out, not_3_out, not_4_out, or_1_out,
       or_2_out, or_3_out, or_4_out;

  not not_1 (not_1_out, ADD);
  not not_2 (not_2_out, SUB);
  not not_3 (not_3_out, OUTT);
  not not_4 (not_4_out, HALT);
  and and_1 (and_1_out, ADD, not_2_out, not_3_out, not_4_out);
  and and_2 (and_2_out, not_1_out, SUB, not_3_out, not_4_out);
  and and_3 (and_3_out, not_1_out, not_2_out, OUTT, not_4_out);
  and and_4 (and_4_out, not_1_out, not_2_out, not_3_out, HALT);
  // AND_Gate and_5 is placed but not wired
  or or_1 (or_1_out, and_1_out, and_4_out);
  or or_2 (or_2_out, and_2_out, and_3_out, and_4_out);
  or or_3 (or_3_out, and_3_out, and_4_out);
  or or_4 (or_4_out, and_3_out, and_4_out);
  SR_LATCH sr_latch_1 (.R(LDA_RESET), .S(or_1_out), .Q(d0));  // open: NQ
  SR_LATCH sr_latch_2 (.R(LDA_RESET), .S(or_2_out), .Q(d1));  // open: NQ
  SR_LATCH sr_latch_3 (.R(LDA_RESET), .S(or_3_out), .Q(d2));  // open: NQ
  SR_LATCH sr_latch_4 (.R(LDA_RESET), .S(or_4_out), .Q(d3));  // open: NQ

  assign ram_write = WRITE;
endmodule

module SR_LATCH (
  input  R,
  input  S,
  output Q,
  output NQ
);

  nor nor_1 (Q, R, NQ);
  nor nor_2 (NQ, Q, S);
endmodule

module ZF (
  input  alu,
  input  clk,
  input  reset,
  output zero,
  output to_cu
);

  D_Flip_Flop d_ff_1 (.D(alu), .clk(clk), .Q(to_cu), .reset(reset));  // open: Qn, preset

  assign zero = to_cu;
endmodule
